# Fritzing sketch cb_test_1 (saved by Fritzing 1.0.1rc)
circuit board: 8.46667cm x 5.64444cm
breadboards: 1

parts:
  Q1 = TRANSISTOR_NPN [part_number=BC182 package=to-92]
  LED1 = LED - 3mm [color="Red (635nm)" current=0.030 package="3 mm [THT]"]
  U1 = RELAY [package=OJ]
  A1 = ESP32-S3 zero
  R1 = Resistor [tolerance=±5% power=0.25W resistance=4.7k package=THT]
  R2 = Resistor [tolerance=±5% power=0.25 resistance=1k package=THT]  # not connected
  R3 = Resistor [tolerance=±5% power=0.25W resistance=4.7k package=THT]  # not connected
  Q2 = TRANSISTOR_NPN [part_number=BC182 package=to-92]
  R4 = Resistor [tolerance=±5% power=0.25W resistance=4.7k package=THT]
  R5 = Resistor [tolerance=±5% power=0.25W resistance=4.7k package=THT]
  R6 = Resistor [tolerance=±5% power=0.25 resistance=1k package=THT]  # not connected
  LED4 = LED - 3mm [color="Red (635nm)" current=0.030 package="3 mm [THT]"]
  U2 = RELAY [package=OJ]
  J3_-_Rugó_feszes = Screw terminal - 2 pins [package=THT]
  J1_-_BE = Screw terminal - 2 pins [package=THT]
  S1 = Momentary Switch [package=tactile-pth]
  F1 = Resettable Fuse PTC [package=0603]
  J2_-_KI = Screw terminal - 2 pins [package=THT]
  F2 = Resettable Fuse PTC [package=0603]

nets:
  N1: Q1.E, LED1.cathode, A1.Pin_2, R1.Pin_0, Q2.E, R4.Pin_1, LED4.cathode, J3_-_Rugó_feszes.pin2, S1.3
  N2: Q1.C, U1.COIL1
  N3: U1.COIL2, A1.Pin_3, U2.COIL1
  N4: U1.MAIN, J1_-_BE.pin1
  N5: U1.NO, F1.2
  N6: A1.Pin_5, R5.Pin_0
  N7: A1.Pin_6, J3_-_Rugó_feszes.pin1, S1.1
  N8: Q2.C, U2.COIL2
  N9: U2.MAIN, J2_-_KI.pin1
  N10: U2.NO, F2.2

custom parts:
  ESP32-S3 zero: ESP32-S3 Mini Development Board, Based on ESP32-S3FH4R2 Dual-Core Processor, 240MHz Running Frequency, 2.4GHz Wi-Fi & Bluetooth 5.
